// Logisim project eight_to_one_mux.circ as structural Verilog: 1 circuit, main circuit main
module main (
  input  s2,
  input  i0,
  input  i1,
  input  i2,
  input  i3,
  input  s0,
  input  s1,
  input  i4,
  input  i5,
  input  i6,
  input  i7
);

  wire and_1_out, and_2_out, multiplexer_1_out, multiplexer_2_out, not_1_out, or_1_out;

  Multiplexer #(.select(2)) multiplexer_1 (
    .in0(i0), .in1(i1), .in2(i2), .in3(i2), .out(multiplexer_1_out), .sel({s1, s0}));
  Multiplexer #(.select(2)) multiplexer_2 (
    .in0(i4), .in1(i5), .in2(i6), .in3(i7), .out(multiplexer_2_out), .sel({s1, s0}));
  not not_1 (not_1_out, s2);
  and and_1 (and_1_out, multiplexer_1_out, not_1_out);
  and and_2 (and_2_out, multiplexer_2_out, s2);
  or or_1 (or_1_out, and_1_out, and_2_out);
  LED y (.in(or_1_out));

  assign i3 = i2;
endmodule
