// Logisim project lab_function.circ as structural Verilog: 1 circuit, main circuit main
module main (
  input  C,
  input  B,
  input  A
);

  wire multiplexer_1_out;

  Multiplexer #(.select(3)) multiplexer_1 (
    .in0(1'b0), .in1(1'b1), .in2(1'b0), .in3(1'b1), .in4(1'b1), .in5(1'b0), .in6(1'b1), .in7(1'b0),
    .out(multiplexer_1_out), .sel({A, B, C}));
  LED F (.in(multiplexer_1_out));
endmodule
